// Logisim project SchemesForExam.circ as structural Verilog
module HS (
  input  A,
  input  B,
  output S,
  output C
);

  xor xor_1 (S, A, B);
  and and_1 (C, A, B);
endmodule

module FA (
  input  Cin,
  input  A,
  input  B,
  output S,
  output C
);

  wire hs_1_c, hs_1_s, hs_2_c;

  HS hs_1 (.A(A), .B(B), .S(hs_1_s), .C(hs_1_c));
  HS hs_2 (.A(Cin), .B(hs_1_s), .S(S), .C(hs_2_c));
  or or_1 (C, hs_2_c, hs_1_c);
endmodule
