// Logisim project BST_2502_Kochkin_lab2_task1.circ as structural Verilog: 2 circuits, main circuit main
module main (
  input  x1,
  input  x2,
  input  x3,
  input  x4,
  output f
);

  wire and_1_out, and_2_out, and_3_out, and_4_out, and_5_out, and_6_out, and_7_out, and_8_out, not_1_out,
       not_2_out, not_3_out, or_1_out, or_2_out;

  not not_1 (not_1_out, x2);
  not not_2 (not_2_out, x3);
  not not_3 (not_3_out, x4);
  and and_1 (and_1_out, not_1_out, not_2_out);
  and and_2 (and_2_out, x2, x3);
  and and_3 (and_3_out, x1, x2);
  and and_4 (and_4_out, x1, not_1_out);
  and and_5 (and_5_out, and_1_out, not_3_out);
  and and_6 (and_6_out, and_2_out, x4);
  and and_7 (and_7_out, and_3_out, x3);
  and and_8 (and_8_out, and_4_out, x4);
  or or_1 (or_1_out, and_5_out, and_6_out);
  or or_2 (or_2_out, and_7_out, and_8_out);
  or or_3 (f, or_1_out, or_2_out);
endmodule

module main_simplified (
  input  x1,
  input  x2,
  input  x3,
  input  x4,
  output f
);

  wire not_1_out, not_2_out, or_1_out;

  not not_1 (not_1_out, x1);
  not not_2 (not_2_out, x3);
  or or_1 (or_1_out, not_1_out, not_2_out);
  or or_2 (f, or_1_out, x4);
endmodule
