// Logisim project BST_2502_Kochkin_lab3_task3.circ as structural Verilog: 1 circuit, main circuit main
module main (
  input  x0,
  input  x1,
  input  x2,
  input  x3,
  output y0,
  output y1
);

  wire and_1_out, not_1_out;

  or or_1 (y0, x3, x2);
  and and_1 (and_1_out, x1, not_1_out);
  not not_1 (not_1_out, x2);
  or or_2 (y1, x3, and_1_out);
endmodule
